// Logisim project noname.circ as structural Verilog: 7 circuits, main circuit цифра - индикатор
module \цифра___индикатор  (
  input  [3:0] \вход ,
  output w1,
  output w2,
  output w3,
  output w4,
  output w5,
  output w6,
  output w7
);

  wire and_1_out, and_2_out, and_3_out, and_4_out, and_5_out, and_6_out, and_7_out, and_8_out, and_9_out,
       and_10_out, and_11_out, and_12_out, and_13_out, and_14_out, and_15_out, and_16_out, and_17_out,
       and_18_out, and_19_out, and_20_out, and_21_out, and_22_out, and_23_out, and_24_out, and_25_out,
       and_26_out, and_27_out, and_28_out, and_29_out, and_30_out, and_31_out, and_32_out, and_33_out,
       and_34_out, and_35_out, not_1_out, not_2_out, not_3_out, not_4_out, not_5_out, not_6_out, not_7_out,
       not_8_out, not_9_out, not_10_out, not_11_out, not_12_out, not_13_out, not_14_out, not_15_out,
       not_16_out, not_17_out, not_18_out, not_19_out, not_20_out, not_21_out, not_22_out, not_23_out,
       not_24_out, not_25_out, not_26_out, not_27_out, not_28_out, not_29_out, not_30_out, not_31_out,
       not_32_out, not_33_out, not_34_out, not_35_out, not_36_out, not_37_out, not_38_out, not_39_out,
       not_40_out, not_41_out, not_42_out, not_43_out;

  not not_1 (not_1_out, \вход [2]);
  and and_1 (and_1_out, not_1_out, \вход [1]);
  and and_2 (and_2_out, \вход [1], not_2_out);
  not not_2 (not_2_out, \вход [0]);
  not not_3 (not_3_out, \вход [3]);
  and and_3 (and_3_out, not_3_out, \вход [2], not_4_out);
  not not_4 (not_4_out, \вход [1]);
  and and_4 (and_4_out, \вход [3], not_5_out);
  not not_5 (not_5_out, \вход [2]);
  and and_5 (and_5_out, \вход [3], \вход [0]);
  not not_6 (not_6_out, \вход [1]);
  and and_6 (and_6_out, not_6_out, not_7_out);
  not not_7 (not_7_out, \вход [0]);
  not not_8 (not_8_out, \вход [3]);
  and and_7 (and_7_out, not_8_out, \вход [2], not_9_out);
  not not_9 (not_9_out, \вход [1]);
  and and_8 (and_8_out, \вход [2], not_10_out);
  not not_10 (not_10_out, \вход [0]);
  and and_9 (and_9_out, \вход [3], not_11_out);
  not not_11 (not_11_out, \вход [2]);
  and and_10 (and_10_out, \вход [3], \вход [1]);
  not not_12 (not_12_out, \вход [2]);
  and and_11 (and_11_out, not_12_out, not_13_out);
  not not_13 (not_13_out, \вход [0]);
  not not_14 (not_14_out, \вход [3]);
  and and_12 (and_12_out, not_14_out, \вход [1]);
  not not_15 (not_15_out, \вход [3]);
  and and_13 (and_13_out, not_15_out, \вход [2], \вход [0]);
  and and_14 (and_14_out, \вход [2], \вход [1]);
  and and_15 (and_15_out, \вход [3], not_16_out, not_17_out);
  not not_16 (not_16_out, \вход [2]);
  not not_17 (not_17_out, \вход [1]);
  and and_16 (and_16_out, \вход [3], not_18_out);
  not not_18 (not_18_out, \вход [0]);
  not not_19 (not_19_out, \вход [3]);
  and and_17 (and_17_out, not_19_out, not_20_out);
  not not_20 (not_20_out, \вход [2]);
  not not_21 (not_21_out, \вход [3]);
  and and_18 (and_18_out, not_21_out, not_22_out, not_23_out);
  not not_22 (not_22_out, \вход [1]);
  not not_23 (not_23_out, \вход [0]);
  not not_24 (not_24_out, \вход [2]);
  and and_19 (and_19_out, not_24_out, not_25_out);
  not not_25 (not_25_out, \вход [0]);
  not not_26 (not_26_out, \вход [3]);
  and and_20 (and_20_out, not_26_out, \вход [1], \вход [0]);
  not not_27 (not_27_out, \вход [1]);
  and and_21 (and_21_out, \вход [3], not_27_out, \вход [0]);
  not not_28 (not_28_out, \вход [2]);
  and and_22 (and_22_out, not_28_out, not_29_out);
  not not_29 (not_29_out, \вход [0]);
  and and_23 (and_23_out, \вход [1], not_30_out);
  not not_30 (not_30_out, \вход [0]);
  and and_24 (and_24_out, \вход [3], \вход [1]);
  and and_25 (and_25_out, \вход [3], \вход [2]);
  not not_31 (not_31_out, \вход [3]);
  not not_32 (not_32_out, \вход [2]);
  and and_26 (and_26_out, not_31_out, not_32_out, not_33_out);
  not not_33 (not_33_out, \вход [0]);
  not not_34 (not_34_out, \вход [2]);
  and and_27 (and_27_out, not_34_out, \вход [1], \вход [0]);
  not not_35 (not_35_out, \вход [1]);
  and and_28 (and_28_out, \вход [2], not_35_out, \вход [0]);
  and and_29 (and_29_out, \вход [2], \вход [1], not_36_out);
  not not_36 (not_36_out, \вход [0]);
  and and_30 (and_30_out, \вход [3], not_37_out);
  not not_37 (not_37_out, \вход [1]);
  not not_38 (not_38_out, \вход [3]);
  and and_31 (and_31_out, not_38_out, not_39_out);
  not not_39 (not_39_out, \вход [1]);
  not not_40 (not_40_out, \вход [3]);
  and and_32 (and_32_out, not_40_out, \вход [0]);
  not not_41 (not_41_out, \вход [1]);
  and and_33 (and_33_out, not_41_out, \вход [0]);
  not not_42 (not_42_out, \вход [3]);
  and and_34 (and_34_out, not_42_out, \вход [2]);
  and and_35 (and_35_out, \вход [3], not_43_out);
  not not_43 (not_43_out, \вход [2]);
  or or_1 (w1, and_1_out, and_2_out, and_3_out, and_4_out, and_5_out);
  or or_2 (w2, and_6_out, and_7_out, and_8_out, and_9_out, and_10_out);
  or or_3 (w4, and_17_out, and_18_out, and_19_out, and_20_out, and_21_out);
  or or_4 (w5, and_22_out, and_23_out, and_24_out, and_25_out);
  or or_5 (w6, and_26_out, and_27_out, and_28_out, and_29_out, and_30_out);
  or or_6 (w7, and_31_out, and_32_out, and_33_out, and_34_out, and_35_out);
  or or_7 (w3, and_11_out, and_12_out, and_13_out, and_14_out, and_15_out, and_16_out);

  // Notes on the sheet:
  //   на входе цифра в двоичном представлении
  //   выводится на 7-сегментном индикаторе
endmodule

module \двоичное_на_индикаторы_поразрядно  (
  input  [31:0] \вход ,
  output [3:0] _7,
  output [3:0] _6,
  output [3:0] _5,
  output [3:0] _4,
  output [3:0] _3,
  output [3:0] _2,
  output [3:0] _1,
  output [3:0] _0
);

  wire [3:0] divider_7_rem, divider_7_rem_2, divider_7_rem_3, divider_7_rem_4, divider_7_rem_5,
       divider_7_rem_6, divider_7_rem_7;
  wire [31:0] divider_1_rem, divider_2_rem, divider_3_rem, divider_4_rem, divider_5_rem, divider_6_rem;
  wire [31:4] divider_1_out, divider_2_out, divider_3_out, divider_4_out, divider_5_out, divider_6_out,
       divider_7_out;

  // Probe on \вход 
  // Probe on _7
  Divider #(.width(32)) divider_1 (
    .a(\вход ), .b(32'h989680), .out({divider_1_out, _7}), .rem(divider_1_rem));  // open: upper
  // Probe on _6
  // Probe on {divider_2_out, _6}
  Divider #(.width(32)) divider_2 (
    .a(divider_1_rem), .b(32'hf4240), .out({divider_2_out, _6}), .rem(divider_2_rem));  // open: upper
  // Probe on _5
  // Probe on {divider_3_out, _5}
  Divider #(.width(32)) divider_3 (
    .a(divider_2_rem), .b(32'h186a0), .out({divider_3_out, _5}), .rem(divider_3_rem));  // open: upper
  // Probe on _4
  Divider #(.width(32)) divider_4 (
    .a(divider_3_rem), .b(32'h2710), .out({divider_4_out, _4}), .rem(divider_4_rem));  // open: upper
  Divider #(.width(32)) divider_5 (
    .a(divider_4_rem), .b(32'h3e8), .out({divider_5_out, _3}), .rem(divider_5_rem));  // open: upper
  // Probe on _3
  // Probe on _2
  Divider #(.width(32)) divider_6 (
    .a(divider_5_rem), .b(32'h64), .out({divider_6_out, _2}), .rem(divider_6_rem));  // open: upper
  // Probe on _1
  Divider #(.width(32)) divider_7 (
    .a(divider_6_rem), .b(32'ha), .out({divider_7_out, _1}),
    .rem({divider_7_rem_7, divider_7_rem_6, divider_7_rem_5, divider_7_rem_4, divider_7_rem_3, divider_7_rem_2, divider_7_rem, _0}));  // open: upper
  // Probe on _0

  // Notes on the sheet:
  //   вывод числа в десятичной системе поразрядно
  //   правильно работает с 8-разрядными числами
endmodule

module main (
);

  wire _0_out, _1_out, _2_out, _3_out, _4_out, _5_out, _6_out, _7_out, _8_out, _9_out, button_2_out,
       button_3_out, button_4_out, button_5_out, button_out, C_out, CE_out,
       \кнопка_цифра_нажата_цифра_1_нажата_цифра , \цифра_индикатор_1_w1 , \цифра_индикатор_1_w2 ,
       \цифра_индикатор_1_w3 , \цифра_индикатор_1_w4 , \цифра_индикатор_1_w5 , \цифра_индикатор_1_w6 ,
       \цифра_индикатор_1_w7 , \цифра_индикатор_2_w1 , \цифра_индикатор_2_w2 , \цифра_индикатор_2_w3 ,
       \цифра_индикатор_2_w4 , \цифра_индикатор_2_w5 , \цифра_индикатор_2_w6 , \цифра_индикатор_2_w7 ,
       \цифра_индикатор_3_w1 , \цифра_индикатор_3_w2 , \цифра_индикатор_3_w3 , \цифра_индикатор_3_w4 ,
       \цифра_индикатор_3_w5 , \цифра_индикатор_3_w6 , \цифра_индикатор_3_w7 , \цифра_индикатор_4_w1 ,
       \цифра_индикатор_4_w2 , \цифра_индикатор_4_w3 , \цифра_индикатор_4_w4 , \цифра_индикатор_4_w5 ,
       \цифра_индикатор_4_w6 , \цифра_индикатор_4_w7 , \цифра_индикатор_5_w1 , \цифра_индикатор_5_w2 ,
       \цифра_индикатор_5_w3 , \цифра_индикатор_5_w4 , \цифра_индикатор_5_w5 , \цифра_индикатор_5_w6 ,
       \цифра_индикатор_5_w7 , \цифра_индикатор_6_w1 , \цифра_индикатор_6_w2 , \цифра_индикатор_6_w3 ,
       \цифра_индикатор_6_w4 , \цифра_индикатор_6_w5 , \цифра_индикатор_6_w6 , \цифра_индикатор_6_w7 ,
       \цифра_индикатор_7_w1 , \цифра_индикатор_7_w2 , \цифра_индикатор_7_w3 , \цифра_индикатор_7_w4 ,
       \цифра_индикатор_7_w5 , \цифра_индикатор_7_w6 , \цифра_индикатор_7_w7 , \цифра_индикатор_8_w1 ,
       \цифра_индикатор_8_w2 , \цифра_индикатор_8_w3 , \цифра_индикатор_8_w4 , \цифра_индикатор_8_w5 ,
       \цифра_индикатор_8_w6 , \цифра_индикатор_8_w7 ;
  wire [3:0] to_3_1__0, to_3_1__1, to_3_1__2, to_3_1__3, to_3_1__4, to_3_1__5, to_3_1__6, to_3_1__7,
       \кнопка_цифра_нажата_цифра_1_двоичное_представление ;

  Button CE (.out(CE_out));
  Button _1 (.out(_1_out));
  Button _4 (.out(_4_out));
  Button _7 (.out(_7_out));
  to_3 to_3_1 (
    ._0(to_3_1__0), ._1(to_3_1__1), ._2(to_3_1__2), ._3(to_3_1__3), ._4(to_3_1__4), ._5(to_3_1__5),
    ._6(to_3_1__6), ._7(to_3_1__7), .\вход (\кнопка_цифра_нажата_цифра_1_двоичное_представление ),
    .\нажата_цифра (\кнопка_цифра_нажата_цифра_1_нажата_цифра ), .\СЕ (CE_out), .in_5(button_4_out),
    .in_6(button_3_out), .in_7(button_2_out), .in_8(button_out), .in_4(button_5_out), .\С (C_out));
  Button C (.out(C_out));
  \кнопка___цифра___нажата_цифра  \u_кнопка_цифра_нажата_цифра_1  (
    ._0(_0_out), ._1(_1_out), ._2(_2_out), ._3(_3_out), ._4(_4_out), ._5(_5_out), ._6(_6_out), ._7(_7_out),
    ._8(_8_out), ._9(_9_out),
    .\двоичное_представление (\кнопка_цифра_нажата_цифра_1_двоичное_представление ),
    .\нажата_цифра (\кнопка_цифра_нажата_цифра_1_нажата_цифра ));
  Button _2 (.out(_2_out));
  Button _3 (.out(_3_out));
  Button _6 (.out(_6_out));
  Button _5 (.out(_5_out));
  Button _8 (.out(_8_out));
  Button _9 (.out(_9_out));
  Button _0 (.out(_0_out));
  Button button (.out(button_out));
  Button button_2 (.out(button_2_out));
  Button button_3 (.out(button_3_out));
  Button button_4 (.out(button_4_out));
  Button button_5 (.out(button_5_out));
  _7_Segment_Display u_7_segment_display_1 (
    .g(\цифра_индикатор_1_w1 ), .f(\цифра_индикатор_1_w2 ), .a(\цифра_индикатор_1_w3 ),
    .b(\цифра_индикатор_1_w4 ), .e(\цифра_индикатор_1_w5 ), .d(\цифра_индикатор_1_w6 ),
    .c(\цифра_индикатор_1_w7 ));  // open: dp
  \цифра___индикатор  \u_цифра_индикатор_1  (
    .\вход (to_3_1__7), .w1(\цифра_индикатор_1_w1 ), .w2(\цифра_индикатор_1_w2 ),
    .w3(\цифра_индикатор_1_w3 ), .w4(\цифра_индикатор_1_w4 ), .w5(\цифра_индикатор_1_w5 ),
    .w6(\цифра_индикатор_1_w6 ), .w7(\цифра_индикатор_1_w7 ));
  \цифра___индикатор  \u_цифра_индикатор_2  (
    .\вход (to_3_1__6), .w1(\цифра_индикатор_2_w1 ), .w2(\цифра_индикатор_2_w2 ),
    .w3(\цифра_индикатор_2_w3 ), .w4(\цифра_индикатор_2_w4 ), .w5(\цифра_индикатор_2_w5 ),
    .w6(\цифра_индикатор_2_w6 ), .w7(\цифра_индикатор_2_w7 ));
  _7_Segment_Display u_7_segment_display_2 (
    .g(\цифра_индикатор_2_w1 ), .f(\цифра_индикатор_2_w2 ), .a(\цифра_индикатор_2_w3 ),
    .b(\цифра_индикатор_2_w4 ), .e(\цифра_индикатор_2_w5 ), .d(\цифра_индикатор_2_w6 ),
    .c(\цифра_индикатор_2_w7 ));  // open: dp
  _7_Segment_Display u_7_segment_display_3 (
    .g(\цифра_индикатор_3_w1 ), .f(\цифра_индикатор_3_w2 ), .a(\цифра_индикатор_3_w3 ),
    .b(\цифра_индикатор_3_w4 ), .e(\цифра_индикатор_3_w5 ), .d(\цифра_индикатор_3_w6 ),
    .c(\цифра_индикатор_3_w7 ));  // open: dp
  \цифра___индикатор  \u_цифра_индикатор_3  (
    .\вход (to_3_1__5), .w1(\цифра_индикатор_3_w1 ), .w2(\цифра_индикатор_3_w2 ),
    .w3(\цифра_индикатор_3_w3 ), .w4(\цифра_индикатор_3_w4 ), .w5(\цифра_индикатор_3_w5 ),
    .w6(\цифра_индикатор_3_w6 ), .w7(\цифра_индикатор_3_w7 ));
  _7_Segment_Display u_7_segment_display_4 (
    .g(\цифра_индикатор_4_w1 ), .f(\цифра_индикатор_4_w2 ), .a(\цифра_индикатор_4_w3 ),
    .b(\цифра_индикатор_4_w4 ), .e(\цифра_индикатор_4_w5 ), .d(\цифра_индикатор_4_w6 ),
    .c(\цифра_индикатор_4_w7 ));  // open: dp
  \цифра___индикатор  \u_цифра_индикатор_4  (
    .\вход (to_3_1__4), .w1(\цифра_индикатор_4_w1 ), .w2(\цифра_индикатор_4_w2 ),
    .w3(\цифра_индикатор_4_w3 ), .w4(\цифра_индикатор_4_w4 ), .w5(\цифра_индикатор_4_w5 ),
    .w6(\цифра_индикатор_4_w6 ), .w7(\цифра_индикатор_4_w7 ));
  _7_Segment_Display u_7_segment_display_5 (
    .g(\цифра_индикатор_5_w1 ), .f(\цифра_индикатор_5_w2 ), .a(\цифра_индикатор_5_w3 ),
    .b(\цифра_индикатор_5_w4 ), .e(\цифра_индикатор_5_w5 ), .d(\цифра_индикатор_5_w6 ),
    .c(\цифра_индикатор_5_w7 ));  // open: dp
  _7_Segment_Display u_7_segment_display_6 (
    .g(\цифра_индикатор_6_w1 ), .f(\цифра_индикатор_6_w2 ), .a(\цифра_индикатор_6_w3 ),
    .b(\цифра_индикатор_6_w4 ), .e(\цифра_индикатор_6_w5 ), .d(\цифра_индикатор_6_w6 ),
    .c(\цифра_индикатор_6_w7 ));  // open: dp
  \цифра___индикатор  \u_цифра_индикатор_5  (
    .\вход (to_3_1__2), .w1(\цифра_индикатор_5_w1 ), .w2(\цифра_индикатор_5_w2 ),
    .w3(\цифра_индикатор_5_w3 ), .w4(\цифра_индикатор_5_w4 ), .w5(\цифра_индикатор_5_w5 ),
    .w6(\цифра_индикатор_5_w6 ), .w7(\цифра_индикатор_5_w7 ));
  \цифра___индикатор  \u_цифра_индикатор_6  (
    .\вход (to_3_1__3), .w1(\цифра_индикатор_6_w1 ), .w2(\цифра_индикатор_6_w2 ),
    .w3(\цифра_индикатор_6_w3 ), .w4(\цифра_индикатор_6_w4 ), .w5(\цифра_индикатор_6_w5 ),
    .w6(\цифра_индикатор_6_w6 ), .w7(\цифра_индикатор_6_w7 ));
  _7_Segment_Display u_7_segment_display_7 (
    .g(\цифра_индикатор_7_w1 ), .f(\цифра_индикатор_7_w2 ), .a(\цифра_индикатор_7_w3 ),
    .b(\цифра_индикатор_7_w4 ), .e(\цифра_индикатор_7_w5 ), .d(\цифра_индикатор_7_w6 ),
    .c(\цифра_индикатор_7_w7 ));  // open: dp
  \цифра___индикатор  \u_цифра_индикатор_7  (
    .\вход (to_3_1__1), .w1(\цифра_индикатор_7_w1 ), .w2(\цифра_индикатор_7_w2 ),
    .w3(\цифра_индикатор_7_w3 ), .w4(\цифра_индикатор_7_w4 ), .w5(\цифра_индикатор_7_w5 ),
    .w6(\цифра_индикатор_7_w6 ), .w7(\цифра_индикатор_7_w7 ));
  _7_Segment_Display u_7_segment_display_8 (
    .g(\цифра_индикатор_8_w1 ), .f(\цифра_индикатор_8_w2 ), .a(\цифра_индикатор_8_w3 ),
    .b(\цифра_индикатор_8_w4 ), .e(\цифра_индикатор_8_w5 ), .d(\цифра_индикатор_8_w6 ),
    .c(\цифра_индикатор_8_w7 ));  // open: dp
  \цифра___индикатор  \u_цифра_индикатор_8  (
    .\вход (to_3_1__0), .w1(\цифра_индикатор_8_w1 ), .w2(\цифра_индикатор_8_w2 ),
    .w3(\цифра_индикатор_8_w3 ), .w4(\цифра_индикатор_8_w4 ), .w5(\цифра_индикатор_8_w5 ),
    .w6(\цифра_индикатор_8_w6 ), .w7(\цифра_индикатор_8_w7 ));
endmodule

module to_3 (
  input  [3:0] \вход ,
  input  \нажата_цифра ,
  input  \СЕ ,
  input  in_4,
  input  in_5,
  input  in_6,
  input  in_7,
  input  in_8,
  input  \С ,
  output [3:0] _0,
  output [3:0] _1,
  output [3:0] _2,
  output [3:0] _3,
  output [3:0] _4,
  output [3:0] _5,
  output [3:0] _6,
  output [3:0] _7
);

  wire and_1_out, buffer_2_out, buffer_3_out, not_1_out, or_1_out, or_2_out, or_3_out, or_4_out, or_5_out,
       or_6_out, \вычисление_1_конец ;
  wire [3:0] buffer_1_out, controlled_buffer_1_out, controlled_buffer_3_out, controlled_buffer_5_out,
       controlled_buffer_7_out, controlled_buffer_9_out, controlled_buffer_11_out, controlled_buffer_13_out,
       controlled_buffer_15_out, \двоичное_на_индикаторы_поразрядно_1__0 ,
       \двоичное_на_индикаторы_поразрядно_1__1 , \двоичное_на_индикаторы_поразрядно_1__2 ,
       \двоичное_на_индикаторы_поразрядно_1__3 , \двоичное_на_индикаторы_поразрядно_1__4 ,
       \двоичное_на_индикаторы_поразрядно_1__5 , \двоичное_на_индикаторы_поразрядно_1__6 ,
       \двоичное_на_индикаторы_поразрядно_1__7 ;
  wire [31:0] register_9_q, register_10_q, \вычисление_1_результат , \индикаторы_число_1_выход ;

  assign buffer_1_out = \вход ;  // Buffer buffer_1, 4 bits wide
  buf buffer_2 (buffer_2_out, \нажата_цифра );
  buf buffer_3 (buffer_3_out, \СЕ );
  or or_1 (or_1_out, buffer_2_out, or_5_out);
  or or_2 (or_2_out, buffer_2_out, in_4);
  not not_1 (not_1_out, \вычисление_1_конец );
  and and_1 (and_1_out, or_1_out, \вычисление_1_конец );
  assign controlled_buffer_1_out = not_1_out ? buffer_1_out : 4'bz;  // Controlled_Buffer controlled_buffer_1
  assign controlled_buffer_1_out = \вычисление_1_конец  ? \двоичное_на_индикаторы_поразрядно_1__0  : 4'bz;  // Controlled_Buffer controlled_buffer_2
  or or_3 (or_3_out, and_1_out, \С );
  Register #(.width(4)) register_1 (.D(controlled_buffer_1_out), .Q(_0), .clk(or_2_out), .clr(or_4_out));  // open: en
  assign controlled_buffer_3_out = not_1_out ? _0 : 4'bz;  // Controlled_Buffer controlled_buffer_3
  or or_4 (or_4_out, buffer_3_out, or_5_out, or_3_out);
  assign controlled_buffer_3_out = \вычисление_1_конец  ? \двоичное_на_индикаторы_поразрядно_1__1  : 4'bz;  // Controlled_Buffer controlled_buffer_4
  assign controlled_buffer_5_out = not_1_out ? _1 : 4'bz;  // Controlled_Buffer controlled_buffer_5
  Register #(.width(4)) register_2 (.D(controlled_buffer_3_out), .Q(_1), .clk(or_2_out), .clr(or_4_out));  // open: en
  Register #(.width(4)) register_3 (.D(controlled_buffer_5_out), .Q(_2), .clk(or_2_out), .clr(or_4_out));  // open: en
  assign controlled_buffer_5_out = \вычисление_1_конец  ? \двоичное_на_индикаторы_поразрядно_1__2  : 4'bz;  // Controlled_Buffer controlled_buffer_6
  assign controlled_buffer_7_out = not_1_out ? _2 : 4'bz;  // Controlled_Buffer controlled_buffer_7
  assign controlled_buffer_7_out = \вычисление_1_конец  ? \двоичное_на_индикаторы_поразрядно_1__3  : 4'bz;  // Controlled_Buffer controlled_buffer_8
  Register #(.width(4)) register_4 (.D(controlled_buffer_7_out), .Q(_3), .clk(or_2_out), .clr(or_4_out));  // open: en
  assign controlled_buffer_9_out = not_1_out ? _3 : 4'bz;  // Controlled_Buffer controlled_buffer_9
  assign controlled_buffer_9_out = \вычисление_1_конец  ? \двоичное_на_индикаторы_поразрядно_1__4  : 4'bz;  // Controlled_Buffer controlled_buffer_10
  or or_5 (or_5_out, in_5, in_6, in_7, in_8);
  Register #(.width(4)) register_5 (.D(controlled_buffer_9_out), .Q(_4), .clk(or_2_out), .clr(or_4_out));  // open: en
  assign controlled_buffer_11_out = not_1_out ? _4 : 4'bz;  // Controlled_Buffer controlled_buffer_11
  Register #(.width(4)) register_6 (.D(controlled_buffer_11_out), .Q(_5), .clk(or_2_out), .clr(or_4_out));  // open: en
  assign controlled_buffer_11_out = \вычисление_1_конец  ? \двоичное_на_индикаторы_поразрядно_1__5  : 4'bz;  // Controlled_Buffer controlled_buffer_12
  \вычисление  \u_вычисление_1  (
    .in_1(in_4), .in_2(in_5), .in_3(in_6), .in_4(in_7), .in_5(in_8), .\_1е (register_10_q),
    .\_2е (register_9_q), .\результат (\вычисление_1_результат ), .\конец (\вычисление_1_конец ),
    .\сброс_операции (or_3_out));
  assign controlled_buffer_13_out = not_1_out ? _5 : 4'bz;  // Controlled_Buffer controlled_buffer_13
  assign controlled_buffer_13_out = \вычисление_1_конец  ? \двоичное_на_индикаторы_поразрядно_1__6  : 4'bz;  // Controlled_Buffer controlled_buffer_14
  Register #(.width(4)) register_7 (.D(controlled_buffer_13_out), .Q(_6), .clk(or_2_out), .clr(or_4_out));  // open: en
  assign controlled_buffer_15_out = not_1_out ? _6 : 4'bz;  // Controlled_Buffer controlled_buffer_15
  assign controlled_buffer_15_out = \вычисление_1_конец  ? \двоичное_на_индикаторы_поразрядно_1__7  : 4'bz;  // Controlled_Buffer controlled_buffer_16
  or or_6 (or_6_out, or_2_out, or_5_out);
  \двоичное_на_индикаторы_поразрядно  \u_двоичное_на_индикаторы_поразрядно_1  (
    .\вход (\вычисление_1_результат ), ._7(\двоичное_на_индикаторы_поразрядно_1__7 ),
    ._6(\двоичное_на_индикаторы_поразрядно_1__6 ), ._5(\двоичное_на_индикаторы_поразрядно_1__5 ),
    ._4(\двоичное_на_индикаторы_поразрядно_1__4 ), ._3(\двоичное_на_индикаторы_поразрядно_1__3 ),
    ._2(\двоичное_на_индикаторы_поразрядно_1__2 ), ._1(\двоичное_на_индикаторы_поразрядно_1__1 ),
    ._0(\двоичное_на_индикаторы_поразрядно_1__0 ));
  Register #(.width(4)) register_8 (.D(controlled_buffer_15_out), .Q(_7), .clk(or_2_out), .clr(or_4_out));  // open: en
  // Probe on \индикаторы_число_1_выход 
  \индикаторы___число  \u_индикаторы_число_1  (
    ._0(_0), ._1(_1), ._2(_2), ._3(_3), ._4(_4), ._5(_5), ._6(_6), ._7(_7),
    .\выход (\индикаторы_число_1_выход ));
  Register #(.width(32), .trigger("falling")) register_9 (
    .D(\индикаторы_число_1_выход ), .Q(register_9_q), .clk(or_6_out), .clr(or_4_out));  // open: en
  // Probe on register_9_q
  Register #(.width(32)) register_10 (.D(register_9_q), .Q(register_10_q), .clk(or_5_out), .clr(or_3_out));  // open: en

  // Notes on the sheet:
  //   при нажатии = вычисляется результат и выводится на индикаторы
  //   тут регистры нужны, чтобы перемещать разряды по мере ввода
  //   если какая-то операция прожата, то обнуляется индикатор и запоминается введенное число
  //   число, которое вводится, сразу запоминается
endmodule

module \кнопка___цифра___нажата_цифра  (
  input  _0,
  input  _1,
  input  _2,
  input  _3,
  input  _4,
  input  _5,
  input  _6,
  input  _7,
  input  _8,
  input  _9,
  output [3:0] \двоичное_представление ,
  output \нажата_цифра 
);

  assign \двоичное_представление  = _0 ? 4'b0000 : 4'bz;  // Controlled_Buffer controlled_buffer_1
  assign \двоичное_представление  = _1 ? 4'b0001 : 4'bz;  // Controlled_Buffer controlled_buffer_2
  assign \двоичное_представление  = _2 ? 4'b0010 : 4'bz;  // Controlled_Buffer controlled_buffer_3
  assign \двоичное_представление  = _3 ? 4'b0011 : 4'bz;  // Controlled_Buffer controlled_buffer_4
  assign \двоичное_представление  = _4 ? 4'b0100 : 4'bz;  // Controlled_Buffer controlled_buffer_5
  assign \двоичное_представление  = _5 ? 4'b0101 : 4'bz;  // Controlled_Buffer controlled_buffer_6
  assign \двоичное_представление  = _6 ? 4'b0110 : 4'bz;  // Controlled_Buffer controlled_buffer_7
  assign \двоичное_представление  = _7 ? 4'b0111 : 4'bz;  // Controlled_Buffer controlled_buffer_8
  assign \двоичное_представление  = _8 ? 4'b1000 : 4'bz;  // Controlled_Buffer controlled_buffer_9
  assign \двоичное_представление  = _9 ? 4'b1001 : 4'bz;  // Controlled_Buffer controlled_buffer_10
  or or_1 (\нажата_цифра , _9, _8, _7, _6, _5, _4, _3, _2, _1, _0);
endmodule

module \индикаторы___число  (
  input  [3:0] _0,
  input  [3:0] _1,
  input  [3:0] _2,
  input  [3:0] _3,
  input  [3:0] _4,
  input  [3:0] _5,
  input  [3:0] _6,
  input  [3:0] _7,
  output [31:0] \выход 
);

  wire [31:0] adder_1_out, adder_2_out, adder_3_out, adder_4_out, adder_5_out, adder_6_out,
       bit_extender_1_out, bit_extender_2_out, bit_extender_3_out, bit_extender_4_out, bit_extender_5_out,
       bit_extender_6_out, bit_extender_7_out, bit_extender_8_out, multiplier_1_cout, multiplier_1_out,
       multiplier_2_cout, multiplier_2_out, multiplier_3_cout, multiplier_3_out, multiplier_4_cout,
       multiplier_4_out, multiplier_5_cout, multiplier_5_out, multiplier_6_cout, multiplier_6_out,
       multiplier_7_cout, multiplier_7_out, multiplier_8_out;

  assign bit_extender_1_out = {{28{1'b0}}, _0};  // Bit_Extender bit_extender_1
  assign bit_extender_2_out = {{28{1'b0}}, _1};  // Bit_Extender bit_extender_2
  assign bit_extender_3_out = {{28{1'b0}}, _2};  // Bit_Extender bit_extender_3
  assign bit_extender_4_out = {{28{1'b0}}, _3};  // Bit_Extender bit_extender_4
  assign bit_extender_5_out = {{28{1'b0}}, _4};  // Bit_Extender bit_extender_5
  assign bit_extender_6_out = {{28{1'b0}}, _5};  // Bit_Extender bit_extender_6
  assign bit_extender_7_out = {{28{1'b0}}, _6};  // Bit_Extender bit_extender_7
  assign bit_extender_8_out = {{28{1'b0}}, _7};  // Bit_Extender bit_extender_8
  Multiplier #(.width(32)) multiplier_1 (
    .a(bit_extender_1_out), .b(32'h1), .out(multiplier_1_out), .cout(multiplier_1_cout));  // open: cin
  Multiplier #(.width(32)) multiplier_2 (
    .a(bit_extender_2_out), .b(32'ha), .out(multiplier_2_out), .cin(multiplier_1_cout),
    .cout(multiplier_2_cout));
  Multiplier #(.width(32)) multiplier_3 (
    .a(bit_extender_3_out), .b(32'h64), .out(multiplier_3_out), .cin(multiplier_2_cout),
    .cout(multiplier_3_cout));
  Multiplier #(.width(32)) multiplier_4 (
    .a(bit_extender_4_out), .b(32'h3e8), .out(multiplier_4_out), .cin(multiplier_3_cout),
    .cout(multiplier_4_cout));
  Multiplier #(.width(32)) multiplier_5 (
    .a(bit_extender_5_out), .b(32'h2710), .out(multiplier_5_out), .cin(multiplier_4_cout),
    .cout(multiplier_5_cout));
  Multiplier #(.width(32)) multiplier_6 (
    .a(bit_extender_6_out), .b(32'h186a0), .out(multiplier_6_out), .cin(multiplier_5_cout),
    .cout(multiplier_6_cout));
  Multiplier #(.width(32)) multiplier_7 (
    .a(bit_extender_7_out), .b(32'hf4240), .out(multiplier_7_out), .cin(multiplier_6_cout),
    .cout(multiplier_7_cout));
  Multiplier #(.width(32)) multiplier_8 (
    .a(bit_extender_8_out), .b(32'h989680), .out(multiplier_8_out), .cin(multiplier_7_cout));  // open: cout
  Adder #(.width(32)) adder_1 (.a(multiplier_1_out), .b(multiplier_2_out), .out(adder_1_out));  // open: cin, cout
  Adder #(.width(32)) adder_2 (.a(multiplier_3_out), .b(multiplier_4_out), .out(adder_2_out));  // open: cin, cout
  Adder #(.width(32)) adder_3 (.a(adder_1_out), .b(adder_2_out), .out(adder_3_out));  // open: cin, cout
  Adder #(.width(32)) adder_4 (.a(adder_3_out), .b(multiplier_5_out), .out(adder_4_out));  // open: cin, cout
  Adder #(.width(32)) adder_5 (.a(multiplier_7_out), .b(multiplier_8_out), .out(adder_5_out));  // open: cin, cout
  Adder #(.width(32)) adder_6 (.a(adder_4_out), .b(multiplier_6_out), .out(adder_6_out));  // open: cin, cout
  Adder #(.width(32)) adder_7 (.a(adder_6_out), .b(adder_5_out), .out(\выход ));  // open: cin, cout

  // Notes on the sheet:
  //   собирает цифры, переведенные в двоичную систему
  //   в число
endmodule

module \вычисление  (
  input  in_1,
  input  in_2,
  input  in_3,
  input  in_4,
  input  in_5,
  input  \сброс_операции ,
  input  [31:0] \_1е ,
  input  [31:0] \_2е ,
  output [31:0] \результат ,
  output \конец 
);

  wire and_1_out, and_2_out, and_3_out, and_4_out, and_5_out, buffer_1_out, buffer_2_out, buffer_3_out,
       buffer_4_out, buffer_5_out, d_ff_1_q, d_ff_2_q, d_ff_3_q, d_ff_4_q, d_ff_5_q, not_1_out, or_1_out;
  wire [31:0] adder_1_out, controlled_buffer_1_out, divider_1_out, multiplier_1_out, subtractor_1_out;

  D_Flip_Flop d_ff_1 (.clk(in_1), .D(in_1), .Q(d_ff_1_q), .reset(\сброс_операции ));  // open: Qn, preset, en
  D_Flip_Flop d_ff_2 (.clk(in_2), .D(in_2), .Q(d_ff_2_q), .reset(\сброс_операции ));  // open: Qn, preset, en
  D_Flip_Flop d_ff_3 (.clk(in_3), .D(in_3), .Q(d_ff_3_q), .reset(\сброс_операции ));  // open: Qn, preset, en
  D_Flip_Flop d_ff_4 (.clk(in_4), .D(in_4), .Q(d_ff_4_q), .reset(\сброс_операции ));  // open: Qn, preset, en
  D_Flip_Flop d_ff_5 (.clk(in_5), .D(in_5), .Q(d_ff_5_q), .reset(\сброс_операции ));  // open: Qn, preset, en
  or or_1 (or_1_out, d_ff_2_q, d_ff_3_q, d_ff_4_q, d_ff_5_q);
  and and_1 (and_1_out, d_ff_1_q, not_1_out);
  not not_1 (not_1_out, or_1_out);
  // Probe on \_1е 
  // Probe on \_2е 
  assign controlled_buffer_1_out = and_1_out ? \_1е  : 32'bz;  // Controlled_Buffer controlled_buffer_1
  Adder #(.width(32)) adder_1 (.a(\_1е ), .b(\_2е ), .out(adder_1_out));  // open: cin, cout
  Subtractor #(.width(32)) subtractor_1 (.a(\_1е ), .b(\_2е ), .out(subtractor_1_out));  // open: bin, bout
  Multiplier #(.width(32)) multiplier_1 (.a(\_2е ), .b(\_1е ), .out(multiplier_1_out));  // open: cin, cout
  Divider #(.width(32)) divider_1 (.a(\_1е ), .b(\_2е ), .out(divider_1_out));  // open: upper, rem
  buf buffer_1 (buffer_1_out, and_1_out);
  buf buffer_2 (buffer_2_out, and_2_out);
  and and_2 (and_2_out, d_ff_2_q, d_ff_1_q);
  assign controlled_buffer_1_out = and_2_out ? adder_1_out : 32'bz;  // Controlled_Buffer controlled_buffer_2
  buf buffer_3 (buffer_3_out, and_3_out);
  and and_3 (and_3_out, d_ff_3_q, d_ff_1_q);
  assign controlled_buffer_1_out = and_3_out ? subtractor_1_out : 32'bz;  // Controlled_Buffer controlled_buffer_3
  buf buffer_4 (buffer_4_out, and_4_out);
  and and_4 (and_4_out, d_ff_4_q, d_ff_1_q);
  assign controlled_buffer_1_out = and_4_out ? multiplier_1_out : 32'bz;  // Controlled_Buffer controlled_buffer_4
  buf buffer_5 (buffer_5_out, and_5_out);
  and and_5 (and_5_out, d_ff_5_q, d_ff_1_q);
  assign controlled_buffer_1_out = and_5_out ? divider_1_out : 32'bz;  // Controlled_Buffer controlled_buffer_5
  // Probe on controlled_buffer_1_out
  or or_2 (\конец , buffer_1_out, buffer_2_out, buffer_3_out, buffer_4_out, buffer_5_out);
  Register #(.width(32)) register_1 (.D(controlled_buffer_1_out), .Q(\результат ), .clk(\конец ));  // open: en, clr

  // Notes on the sheet:
  //   сбрасывает операции, но не числа
  //   осуществляет операции над числами
endmodule
